// Logisim project cpu.circ as structural Verilog: 9 circuits, main circuit main
module main (
  input  reset
);

  wire alu_1_zero, ALUinB, and_1_out, and_2_out, blt, bne, clk, DMwe, \input , jal, JP, JR, keyboard_1_avail,
       multiplexer_5_out, not_1_out, not_4_out, \output , Rdst, Rwd, Rwe, sh, srl, tunnel, tunnel_t;
  wire [1:0] ALUop;
  wire [2:0] multiplexer_6_out, multiplexer_8_out, rd, rs, rt, shamt;
  wire [5:0] immed;
  wire [6:0] bit_extender_4_out, keyboard_1_data;
  wire [11:0] addr;
  wire [15:0] address, alu_1_out, ascii, bit_extender_1_out, branch_result, immed_16, instr,
       multiplexer_2_out, multiplexer_3_out, multiplexer_4_out, multiplexer_7_out, multiplexer_9_out,
       multiplexer_10_out, multiplexer_11_out, multiplexer_12_out, n16_bit_register_1_output, PC_1,
       ram_1_data, registerfile_1_out2, rs_t, shifter_1_output;

  Clock clock_1 (.out(clk));
  control u_JR (
    .instruction(instr), .ALUop(ALUop), .JP(JP), .ALUinB(ALUinB), .DMwe(DMwe), .Rwe(Rwe), .Rdst(Rdst),
    .Rwd(Rwd), .immediate(immed), .shamt(shamt), .rd(rd), .rt(rt), .rs(rs), .address(addr), .bne(bne),
    .JR(JR), .sh(sh), .srl(srl), .blt(blt), .jal(jal), .\input (\input ), .\output (\output ));  // open: BR
  _16_bit_register u_16_bit_register_1 (
    .\input (multiplexer_9_out), .clk(clk), .WE(1'b1), .RES(reset), .\output (n16_bit_register_1_output));
  Keyboard keyboard_1 (.clk(clk), .re(\input ), .clr(reset), .avail(keyboard_1_avail), .data(keyboard_1_data));
  full_adder u_PC_1 (.sub(1'b0), .A(16'h1), .B(n16_bit_register_1_output), .result(PC_1));  // open: ovf
  ROM #(.addrWidth(16), .dataWidth(16)) rom_1 (.addr(n16_bit_register_1_output), .data(instr), .sel(1'b1));
  assign bit_extender_1_out = {{9{1'b0}}, keyboard_1_data};  // Bit_Extender bit_extender_1
  // Probe on multiplexer_9_out
  Multiplexer #(.width(16), .disabled(0), .enable("false")) multiplexer_1 (
    .in0(16'h80), .in1(bit_extender_1_out), .out(ascii), .sel(keyboard_1_avail));
  // Probe on ascii
  full_adder branch (.sub(1'b0), .A(PC_1), .B(immed_16), .result(branch_result));  // open: ovf
  and and_1 (and_1_out, tunnel, bne);
  and and_2 (and_2_out, tunnel_t, tunnel);
  Multiplexer #(.width(16), .disabled(0), .enable("false")) multiplexer_2 (
    .in0(multiplexer_10_out), .in1(PC_1), .out(multiplexer_2_out), .sel(jal));
  Multiplexer #(.width(16), .disabled(0), .enable("false")) multiplexer_3 (
    .in0(multiplexer_2_out), .in1(ascii), .out(multiplexer_3_out), .sel(\input ));
  Multiplexer #(.width(16), .disabled(0), .enable("false")) multiplexer_4 (
    .in0(PC_1), .in1(branch_result), .out(multiplexer_4_out), .sel(multiplexer_5_out));
  Multiplexer #(.disabled(0), .enable("false")) multiplexer_5 (
    .in0(and_1_out), .in1(and_2_out), .out(multiplexer_5_out), .sel(blt));
  Multiplexer #(.width(3), .disabled(0), .enable("false")) multiplexer_6 (
    .in0(rd), .in1(3'b111), .out(multiplexer_6_out), .sel(jal));
  Multiplexer #(.width(16), .disabled(0), .enable("false")) multiplexer_7 (
    .in0(address), .in1(rs_t), .out(multiplexer_7_out), .sel(JR));
  not not_1 (not_1_out, clk);
  Multiplexer #(.width(3), .disabled(0), .enable("false")) multiplexer_8 (
    .in0(rt), .in1(multiplexer_6_out), .out(multiplexer_8_out), .sel(Rdst));
  Multiplexer #(.width(16), .disabled(0), .enable("false")) multiplexer_9 (
    .in0(multiplexer_4_out), .in1(multiplexer_7_out), .out(multiplexer_9_out), .sel(JP));
  // Probe on multiplexer_10_out
  RegisterFile registerfile_1 (
    .reset(reset), .clk(not_1_out), .read1(rs), .read2(rt), .RegWriteEnable(Rwe), .write(multiplexer_8_out),
    .data(multiplexer_3_out), .out1(rs_t), .out2(registerfile_1_out2));
  Multiplexer #(.width(16), .disabled(0), .enable("false")) multiplexer_10 (
    .in0(multiplexer_12_out), .in1(shifter_1_output), .out(multiplexer_10_out), .sel(sh));
  // Probe on registerfile_1_out2
  assign immed_16 = {{10{immed[5]}}, immed};  // Bit_Extender bit_extender_2
  assign address = {{4{addr[11]}}, addr};  // Bit_Extender bit_extender_3
  shifter shifter_1 (.\input (rs_t), .srl(srl), .shamt(shamt), .\output (shifter_1_output));
  // Probe on rs_t
  Multiplexer #(.width(16), .disabled(0), .enable("false")) multiplexer_11 (
    .in0(registerfile_1_out2), .in1(immed_16), .out(multiplexer_11_out), .sel(ALUinB));
  Multiplexer #(.width(16), .disabled(0), .enable("false")) multiplexer_12 (
    .in0(alu_1_out), .in1(ram_1_data), .out(multiplexer_12_out), .sel(Rwd));
  ALU alu_1 (.ALUop(ALUop), .InputData1(rs_t), .InputData2(multiplexer_11_out), .zero(alu_1_zero), .out(alu_1_out));
  Bit_Extender #(.in_width(16), .out_width(7)) bit_extender_4 (.in(rs_t), .out(bit_extender_4_out));
  not not_2 (tunnel, alu_1_zero);
  TTY #(.rows(13), .cols(80), .trigger("falling")) tty_1 (
    .data(bit_extender_4_out), .clk(clk), .we(\output ), .clr(reset));
  // Probe on alu_1_out
  not not_3 (tunnel_t, alu_1_out[15]);
  not not_4 (not_4_out, clk);
  RAM #(.addrWidth(16), .dataWidth(16), .bus("separate")) ram_1 (
    .addr(alu_1_out), .din(registerfile_1_out2), .data(ram_1_data), .str(DMwe), .clk(not_4_out));  // open: sel, ld, clr
endmodule

module _16_bit_register (
  input  [15:0] \input ,
  input  clk,
  input  WE,
  input  RES,
  output [15:0] \output 
);

  D_Flip_Flop d_ff_1 (.clk(clk), .D(\input [0]), .Q(\output [0]), .en(WE), .reset(RES));  // open: Qn, preset
  D_Flip_Flop d_ff_2 (.clk(clk), .D(\input [1]), .Q(\output [1]), .en(WE), .reset(RES));  // open: Qn, preset
  D_Flip_Flop d_ff_3 (.clk(clk), .D(\input [2]), .Q(\output [2]), .en(WE), .reset(RES));  // open: Qn, preset
  D_Flip_Flop d_ff_4 (.clk(clk), .D(\input [3]), .Q(\output [3]), .en(WE), .reset(RES));  // open: Qn, preset
  D_Flip_Flop d_ff_5 (.clk(clk), .D(\input [4]), .Q(\output [4]), .en(WE), .reset(RES));  // open: Qn, preset
  D_Flip_Flop d_ff_6 (.clk(clk), .D(\input [5]), .Q(\output [5]), .en(WE), .reset(RES));  // open: Qn, preset
  D_Flip_Flop d_ff_7 (.clk(clk), .D(\input [6]), .Q(\output [6]), .en(WE), .reset(RES));  // open: Qn, preset
  D_Flip_Flop d_ff_8 (.clk(clk), .D(\input [7]), .Q(\output [7]), .en(WE), .reset(RES));  // open: Qn, preset
  D_Flip_Flop d_ff_9 (.clk(clk), .D(\input [8]), .Q(\output [8]), .en(WE), .reset(RES));  // open: Qn, preset
  D_Flip_Flop d_ff_10 (.clk(clk), .D(\input [9]), .Q(\output [9]), .en(WE), .reset(RES));  // open: Qn, preset
  D_Flip_Flop d_ff_11 (.clk(clk), .D(\input [10]), .Q(\output [10]), .en(WE), .reset(RES));  // open: Qn, preset
  D_Flip_Flop d_ff_12 (.clk(clk), .D(\input [11]), .Q(\output [11]), .en(WE), .reset(RES));  // open: Qn, preset
  D_Flip_Flop d_ff_13 (.clk(clk), .D(\input [12]), .Q(\output [12]), .en(WE), .reset(RES));  // open: Qn, preset
  D_Flip_Flop d_ff_14 (.clk(clk), .D(\input [13]), .Q(\output [13]), .en(WE), .reset(RES));  // open: Qn, preset
  D_Flip_Flop d_ff_15 (.clk(clk), .D(\input [14]), .Q(\output [14]), .en(WE), .reset(RES));  // open: Qn, preset
  D_Flip_Flop d_ff_16 (.clk(clk), .D(\input [15]), .Q(\output [15]), .en(WE), .reset(RES));  // open: Qn, preset

  // Other names for the same wires on the sheet: _0 = \input [0]; _1 = \input [1]; _2 = \input [2]; _3 = \input [3];
  //   _4 = \input [4]; _5 = \input [5]; _6 = \input [6]; _7 = \input [7]; _8 = \input [8]; _9 = \input [9];
  //   _10 = \input [10]; _11 = \input [11]; _12 = \input [12]; _13 = \input [13]; _14 = \input [14];
  //   _15 = \input [15]; Q0 = \output [0]; Q1 = \output [1]; Q2 = \output [2]; Q3 = \output [3]; Q4 = \output [4];
  //   Q5 = \output [5]; Q6 = \output [6]; Q7 = \output [7]; Q8 = \output [8]; Q9 = \output [9]; Q10 = \output [10];
  //   Q11 = \output [11]; Q12 = \output [12]; Q13 = \output [13]; Q14 = \output [14]; Q15 = \output [15]
endmodule

module RegisterFile (
  input  reset,
  input  clk,
  input  [2:0] read1,
  input  [2:0] read2,
  input  RegWriteEnable,
  input  [2:0] write,
  input  [15:0] data,
  output [15:0] out1,
  output [15:0] out2
);

  wire decoder_1_out1, decoder_1_out2, decoder_1_out3, decoder_1_out4, decoder_1_out5, decoder_1_out6,
       decoder_1_out7, decoder_2_out0, decoder_2_out1, decoder_2_out2, decoder_2_out3, decoder_2_out4,
       decoder_2_out5, decoder_2_out6, decoder_2_out7, decoder_3_out0, decoder_3_out1, decoder_3_out2,
       decoder_3_out3, decoder_3_out4, decoder_3_out5, decoder_3_out6, decoder_3_out7;
  wire [15:0] n16_bit_register_1_output, n16_bit_register_2_output, n16_bit_register_3_output,
       n16_bit_register_4_output, n16_bit_register_5_output, n16_bit_register_6_output,
       n16_bit_register_7_output, n16_bit_register_8_output;

  Decoder #(.select(3), .disabled(0)) decoder_1 (
    .out1(decoder_1_out1), .out2(decoder_1_out2), .out3(decoder_1_out3), .out4(decoder_1_out4),
    .out5(decoder_1_out5), .out6(decoder_1_out6), .out7(decoder_1_out7), .sel(write), .en(RegWriteEnable));  // open: out0
  _16_bit_register u_16_bit_register_1 (
    .clk(clk), .RES(reset), .\output (n16_bit_register_1_output));  // open: input, WE
  _16_bit_register u_16_bit_register_2 (
    .\input (data), .clk(clk), .WE(decoder_1_out1), .RES(reset), .\output (n16_bit_register_2_output));
  _16_bit_register u_16_bit_register_3 (
    .\input (data), .clk(clk), .WE(decoder_1_out2), .RES(reset), .\output (n16_bit_register_3_output));
  _16_bit_register u_16_bit_register_4 (
    .\input (data), .clk(clk), .WE(decoder_1_out3), .RES(reset), .\output (n16_bit_register_4_output));
  _16_bit_register u_16_bit_register_5 (
    .\input (data), .clk(clk), .WE(decoder_1_out4), .RES(reset), .\output (n16_bit_register_5_output));
  _16_bit_register u_16_bit_register_6 (
    .\input (data), .clk(clk), .WE(decoder_1_out5), .RES(reset), .\output (n16_bit_register_6_output));
  _16_bit_register u_16_bit_register_7 (
    .\input (data), .clk(clk), .WE(decoder_1_out6), .RES(reset), .\output (n16_bit_register_7_output));
  _16_bit_register u_16_bit_register_8 (
    .\input (data), .clk(clk), .WE(decoder_1_out7), .RES(reset), .\output (n16_bit_register_8_output));
  // Probe on n16_bit_register_1_output
  // Probe on n16_bit_register_2_output
  // Probe on n16_bit_register_3_output
  // Probe on n16_bit_register_4_output
  // Probe on n16_bit_register_5_output
  // Probe on n16_bit_register_6_output
  // Probe on n16_bit_register_7_output
  // Probe on n16_bit_register_8_output
  assign out2 = decoder_3_out0 ? n16_bit_register_1_output : 16'bz;  // Controlled_Buffer controlled_buffer_1
  assign out1 = decoder_2_out0 ? n16_bit_register_1_output : 16'bz;  // Controlled_Buffer controlled_buffer_2
  assign out2 = decoder_3_out1 ? n16_bit_register_2_output : 16'bz;  // Controlled_Buffer controlled_buffer_3
  assign out1 = decoder_2_out1 ? n16_bit_register_2_output : 16'bz;  // Controlled_Buffer controlled_buffer_4
  assign out2 = decoder_3_out2 ? n16_bit_register_3_output : 16'bz;  // Controlled_Buffer controlled_buffer_5
  assign out1 = decoder_2_out2 ? n16_bit_register_3_output : 16'bz;  // Controlled_Buffer controlled_buffer_6
  assign out2 = decoder_3_out3 ? n16_bit_register_4_output : 16'bz;  // Controlled_Buffer controlled_buffer_7
  assign out1 = decoder_2_out3 ? n16_bit_register_4_output : 16'bz;  // Controlled_Buffer controlled_buffer_8
  assign out2 = decoder_3_out4 ? n16_bit_register_5_output : 16'bz;  // Controlled_Buffer controlled_buffer_9
  assign out1 = decoder_2_out4 ? n16_bit_register_5_output : 16'bz;  // Controlled_Buffer controlled_buffer_10
  assign out2 = decoder_3_out5 ? n16_bit_register_6_output : 16'bz;  // Controlled_Buffer controlled_buffer_11
  assign out1 = decoder_2_out5 ? n16_bit_register_6_output : 16'bz;  // Controlled_Buffer controlled_buffer_12
  assign out2 = decoder_3_out6 ? n16_bit_register_7_output : 16'bz;  // Controlled_Buffer controlled_buffer_13
  assign out1 = decoder_2_out6 ? n16_bit_register_7_output : 16'bz;  // Controlled_Buffer controlled_buffer_14
  assign out2 = decoder_3_out7 ? n16_bit_register_8_output : 16'bz;  // Controlled_Buffer controlled_buffer_15
  assign out1 = decoder_2_out7 ? n16_bit_register_8_output : 16'bz;  // Controlled_Buffer controlled_buffer_16
  Decoder #(.select(3), .disabled(0), .enable("false")) decoder_2 (
    .out0(decoder_2_out0), .out1(decoder_2_out1), .out2(decoder_2_out2), .out3(decoder_2_out3),
    .out4(decoder_2_out4), .out5(decoder_2_out5), .out6(decoder_2_out6), .out7(decoder_2_out7), .sel(read1));
  Decoder #(.select(3), .disabled(0), .enable("false")) decoder_3 (
    .out0(decoder_3_out0), .out1(decoder_3_out1), .out2(decoder_3_out2), .out3(decoder_3_out3),
    .out4(decoder_3_out4), .out5(decoder_3_out5), .out6(decoder_3_out6), .out7(decoder_3_out7), .sel(read2));
endmodule

module full_adder (
  input  sub,
  input  [15:0] A,
  input  [15:0] B,
  output [15:0] result,
  output ovf
);

  wire n1_bit_adder_1_cout, n1_bit_adder_2_cout, n1_bit_adder_3_cout, n1_bit_adder_4_cout,
       n1_bit_adder_5_cout, n1_bit_adder_6_cout, n1_bit_adder_7_cout, n1_bit_adder_8_cout,
       n1_bit_adder_9_cout, n1_bit_adder_10_cout, n1_bit_adder_11_cout, n1_bit_adder_12_cout,
       n1_bit_adder_13_cout, n1_bit_adder_14_cout, n1_bit_adder_15_cout, n1_bit_adder_16_cout, xor_1_out,
       xor_2_out, xor_3_out, xor_4_out, xor_5_out, xor_6_out, xor_7_out, xor_8_out, xor_9_out, xor_10_out,
       xor_11_out, xor_12_out, xor_13_out, xor_14_out, xor_15_out, xor_16_out;

  xor xor_1 (xor_1_out, B[0], sub);
  xor xor_2 (xor_2_out, B[1], sub);
  xor xor_3 (xor_3_out, B[2], sub);
  xor xor_4 (xor_4_out, B[3], sub);
  xor xor_5 (xor_5_out, B[4], sub);
  xor xor_6 (xor_6_out, B[5], sub);
  xor xor_7 (xor_7_out, B[6], sub);
  xor xor_8 (xor_8_out, B[7], sub);
  xor xor_9 (xor_9_out, B[8], sub);
  xor xor_10 (xor_10_out, B[9], sub);
  xor xor_11 (xor_11_out, B[10], sub);
  xor xor_12 (xor_12_out, B[11], sub);
  xor xor_13 (xor_13_out, B[12], sub);
  xor xor_14 (xor_14_out, B[13], sub);
  xor xor_15 (xor_15_out, B[14], sub);
  xor xor_16 (xor_16_out, B[15], sub);
  _1_bit_adder u_1_bit_adder_1 (.A(A[0]), .B(xor_1_out), .sum(result[0]), .Cin(sub), .Cout(n1_bit_adder_1_cout));
  _1_bit_adder u_1_bit_adder_2 (
    .A(A[1]), .B(xor_2_out), .sum(result[1]), .Cin(n1_bit_adder_1_cout), .Cout(n1_bit_adder_2_cout));
  _1_bit_adder u_1_bit_adder_3 (
    .A(A[2]), .B(xor_3_out), .sum(result[2]), .Cin(n1_bit_adder_2_cout), .Cout(n1_bit_adder_3_cout));
  _1_bit_adder u_1_bit_adder_4 (
    .A(A[3]), .B(xor_4_out), .sum(result[3]), .Cin(n1_bit_adder_3_cout), .Cout(n1_bit_adder_4_cout));
  _1_bit_adder u_1_bit_adder_5 (
    .A(A[4]), .B(xor_5_out), .sum(result[4]), .Cin(n1_bit_adder_4_cout), .Cout(n1_bit_adder_5_cout));
  _1_bit_adder u_1_bit_adder_6 (
    .A(A[5]), .B(xor_6_out), .sum(result[5]), .Cin(n1_bit_adder_5_cout), .Cout(n1_bit_adder_6_cout));
  _1_bit_adder u_1_bit_adder_7 (
    .A(A[6]), .B(xor_7_out), .sum(result[6]), .Cin(n1_bit_adder_6_cout), .Cout(n1_bit_adder_7_cout));
  _1_bit_adder u_1_bit_adder_8 (
    .A(A[7]), .B(xor_8_out), .sum(result[7]), .Cin(n1_bit_adder_7_cout), .Cout(n1_bit_adder_8_cout));
  _1_bit_adder u_1_bit_adder_9 (
    .A(A[8]), .B(xor_9_out), .sum(result[8]), .Cin(n1_bit_adder_8_cout), .Cout(n1_bit_adder_9_cout));
  _1_bit_adder u_1_bit_adder_10 (
    .A(A[9]), .B(xor_10_out), .sum(result[9]), .Cin(n1_bit_adder_9_cout), .Cout(n1_bit_adder_10_cout));
  _1_bit_adder u_1_bit_adder_11 (
    .A(A[10]), .B(xor_11_out), .sum(result[10]), .Cin(n1_bit_adder_10_cout), .Cout(n1_bit_adder_11_cout));
  _1_bit_adder u_1_bit_adder_12 (
    .A(A[11]), .B(xor_12_out), .sum(result[11]), .Cin(n1_bit_adder_11_cout), .Cout(n1_bit_adder_12_cout));
  _1_bit_adder u_1_bit_adder_13 (
    .A(A[12]), .B(xor_13_out), .sum(result[12]), .Cin(n1_bit_adder_12_cout), .Cout(n1_bit_adder_13_cout));
  _1_bit_adder u_1_bit_adder_14 (
    .A(A[13]), .B(xor_14_out), .sum(result[13]), .Cin(n1_bit_adder_13_cout), .Cout(n1_bit_adder_14_cout));
  _1_bit_adder u_1_bit_adder_15 (
    .A(A[14]), .B(xor_15_out), .sum(result[14]), .Cin(n1_bit_adder_14_cout), .Cout(n1_bit_adder_15_cout));
  _1_bit_adder u_1_bit_adder_16 (
    .A(A[15]), .B(xor_16_out), .sum(result[15]), .Cin(n1_bit_adder_15_cout), .Cout(n1_bit_adder_16_cout));
  xor xor_17 (ovf, n1_bit_adder_15_cout, n1_bit_adder_16_cout);
endmodule

module _1_bit_adder (
  input  Cin,
  input  A,
  input  B,
  output sum,
  output Cout
);

  wire and_1_out, and_2_out, xor_1_out;

  and and_1 (and_1_out, A, B);
  xor xor_1 (xor_1_out, A, B);
  and and_2 (and_2_out, Cin, xor_1_out);
  or or_1 (Cout, and_1_out, and_2_out);
  xor xor_2 (sum, Cin, xor_1_out);
endmodule

module ALU (
  input  [1:0] ALUop,
  input  [15:0] InputData1,
  input  [15:0] InputData2,
  output zero,
  output [15:0] out
);

  wire [15:0] add_result, not_1_out, xor_1_out;

  full_adder add (.sub(ALUop[0]), .A(InputData1), .B(InputData2), .result(add_result));  // open: ovf
  assign xor_1_out = InputData1 ^ InputData2;  // XOR_Gate xor_1, 16 bits wide
  assign not_1_out = ~InputData1;  // NOT_Gate not_1, 16 bits wide
  Multiplexer #(.select(2), .width(16), .disabled(0), .enable("false")) multiplexer_1 (
    .in0(add_result), .in1(add_result), .in2(xor_1_out), .in3(not_1_out), .out(out), .sel(ALUop));
  ExactlyOne xor_2 (
    .out(zero), .in0(out[0]), .in1(out[1]), .in2(out[2]), .in3(out[3]), .in4(out[4]), .in5(out[5]),
    .in6(out[6]), .in7(out[7]), .in8(out[8]), .in9(out[9]), .in10(out[10]), .in11(out[11]), .in12(out[12]),
    .in13(out[13]), .in14(out[14]), .in15(out[15]), .in16(1'b1));
endmodule

module control (
  input  [15:0] instruction,
  output [1:0] ALUop,
  output ALUinB,
  output bne,
  output BR,
  output JP,
  output Rwe,
  output DMwe,
  output Rdst,
  output Rwd,
  output JR,
  output sh,
  output srl,
  output blt,
  output jal,
  output \input ,
  output \output ,
  output [5:0] immediate,
  output [2:0] shamt,
  output [2:0] rd,
  output [2:0] rt,
  output [2:0] rs,
  output [11:0] address
);

  wire _0, _1, _2, _3, _4, _6, _11;

  Decoder #(.select(4), .disabled(0), .enable("false")) decoder_1 (
    .out0(_0), .out1(_1), .out2(_2), .out3(_3), .out4(_4), .out5(srl), .out6(_6), .out7(Rwd), .out8(DMwe),
    .out9(bne), .out10(blt), .out11(_11), .out12(JR), .out13(jal), .out14(\input ), .out15(\output ),
    .sel(instruction[15:12]));
  or or_1 (ALUop[0], _2, _3, bne, blt);
  or or_2 (ALUop[1], _3, _4);
  or or_3 (BR, bne, blt);
  or or_4 (JP, _11, JR, jal);
  or or_5 (Rdst, _0, _2, _3, _4, srl, _6, jal);
  or or_6 (sh, srl, _6);
  or or_7 (ALUinB, _1, Rwd, DMwe);
  or or_8 (Rwe, _0, _1, _2, _3, _4, srl, _6, Rwd, jal, \input );

  assign address = instruction[11:0];
  assign immediate = instruction[5:0];
  assign rd = instruction[5:3];
  assign rs = instruction[11:9];
  assign rt = instruction[8:6];
  assign shamt = instruction[2:0];

  // Other names for the same wires on the sheet: _5 = srl; _7 = Rwd; _8 = DMwe; _9 = bne; _10 = blt; _12 = JR;
  //   _13 = jal; _14 = \input ; _15 = \output ; Opcode[3:0] = instruction[15:12]
endmodule

module shift_left (
  input  [15:0] \input ,
  input  [2:0] shamt,
  output [15:0] \output 
);

  wire multiplexer_1_out, multiplexer_2_out, multiplexer_3_out, multiplexer_4_out, multiplexer_5_out,
       multiplexer_6_out, multiplexer_7_out, multiplexer_8_out, multiplexer_9_out, multiplexer_10_out,
       multiplexer_11_out, multiplexer_12_out, multiplexer_13_out, multiplexer_14_out, multiplexer_15_out,
       multiplexer_16_out, multiplexer_17_out, multiplexer_18_out, multiplexer_19_out, multiplexer_20_out,
       multiplexer_21_out, multiplexer_22_out, multiplexer_23_out, multiplexer_24_out, multiplexer_25_out,
       multiplexer_26_out, multiplexer_27_out, multiplexer_28_out, multiplexer_29_out, multiplexer_30_out,
       multiplexer_31_out, multiplexer_32_out;

  Multiplexer #(.disabled(0), .enable("false")) multiplexer_1 (
    .in0(\input [15]), .in1(\input [11]), .out(multiplexer_1_out), .sel(shamt[2]));
  Multiplexer #(.disabled(0), .enable("false")) multiplexer_2 (
    .in0(\input [14]), .in1(\input [10]), .out(multiplexer_2_out), .sel(shamt[2]));
  Multiplexer #(.disabled(0), .enable("false")) multiplexer_3 (
    .in0(\input [13]), .in1(\input [9]), .out(multiplexer_3_out), .sel(shamt[2]));
  Multiplexer #(.disabled(0), .enable("false")) multiplexer_4 (
    .in0(\input [12]), .in1(\input [8]), .out(multiplexer_4_out), .sel(shamt[2]));
  Multiplexer #(.disabled(0), .enable("false")) multiplexer_5 (
    .in0(\input [11]), .in1(\input [7]), .out(multiplexer_5_out), .sel(shamt[2]));
  Multiplexer #(.disabled(0), .enable("false")) multiplexer_6 (
    .in0(\input [10]), .in1(\input [6]), .out(multiplexer_6_out), .sel(shamt[2]));
  Multiplexer #(.disabled(0), .enable("false")) multiplexer_7 (
    .in0(\input [9]), .in1(\input [5]), .out(multiplexer_7_out), .sel(shamt[2]));
  Multiplexer #(.disabled(0), .enable("false")) multiplexer_8 (
    .in0(\input [8]), .in1(\input [4]), .out(multiplexer_8_out), .sel(shamt[2]));
  Multiplexer #(.disabled(0), .enable("false")) multiplexer_9 (
    .in0(\input [7]), .in1(\input [3]), .out(multiplexer_9_out), .sel(shamt[2]));
  Multiplexer #(.disabled(0), .enable("false")) multiplexer_10 (
    .in0(\input [6]), .in1(\input [2]), .out(multiplexer_10_out), .sel(shamt[2]));
  Multiplexer #(.disabled(0), .enable("false")) multiplexer_11 (
    .in0(\input [5]), .in1(\input [1]), .out(multiplexer_11_out), .sel(shamt[2]));
  Multiplexer #(.disabled(0), .enable("false")) multiplexer_12 (
    .in0(\input [4]), .in1(\input [0]), .out(multiplexer_12_out), .sel(shamt[2]));
  Multiplexer #(.disabled(0), .enable("false")) multiplexer_13 (
    .in0(\input [3]), .in1(1'b0), .out(multiplexer_13_out), .sel(shamt[2]));
  Multiplexer #(.disabled(0), .enable("false")) multiplexer_14 (
    .in0(\input [2]), .in1(1'b0), .out(multiplexer_14_out), .sel(shamt[2]));
  Multiplexer #(.disabled(0), .enable("false")) multiplexer_15 (
    .in0(\input [1]), .in1(1'b0), .out(multiplexer_15_out), .sel(shamt[2]));
  Multiplexer #(.disabled(0), .enable("false")) multiplexer_16 (
    .in0(\input [0]), .in1(1'b0), .out(multiplexer_16_out), .sel(shamt[2]));
  Multiplexer #(.disabled(0), .enable("false")) multiplexer_17 (
    .in0(multiplexer_1_out), .in1(multiplexer_3_out), .out(multiplexer_17_out), .sel(shamt[1]));
  Multiplexer #(.disabled(0), .enable("false")) multiplexer_18 (
    .in0(multiplexer_2_out), .in1(multiplexer_4_out), .out(multiplexer_18_out), .sel(shamt[1]));
  Multiplexer #(.disabled(0), .enable("false")) multiplexer_19 (
    .in0(multiplexer_3_out), .in1(multiplexer_5_out), .out(multiplexer_19_out), .sel(shamt[1]));
  Multiplexer #(.disabled(0), .enable("false")) multiplexer_20 (
    .in0(multiplexer_4_out), .in1(multiplexer_6_out), .out(multiplexer_20_out), .sel(shamt[1]));
  Multiplexer #(.disabled(0), .enable("false")) multiplexer_21 (
    .in0(multiplexer_5_out), .in1(multiplexer_7_out), .out(multiplexer_21_out), .sel(shamt[1]));
  Multiplexer #(.disabled(0), .enable("false")) multiplexer_22 (
    .in0(multiplexer_6_out), .in1(multiplexer_8_out), .out(multiplexer_22_out), .sel(shamt[1]));
  Multiplexer #(.disabled(0), .enable("false")) multiplexer_23 (
    .in0(multiplexer_7_out), .in1(multiplexer_9_out), .out(multiplexer_23_out), .sel(shamt[1]));
  Multiplexer #(.disabled(0), .enable("false")) multiplexer_24 (
    .in0(multiplexer_8_out), .in1(multiplexer_10_out), .out(multiplexer_24_out), .sel(shamt[1]));
  Multiplexer #(.disabled(0), .enable("false")) multiplexer_25 (
    .in0(multiplexer_9_out), .in1(multiplexer_11_out), .out(multiplexer_25_out), .sel(shamt[1]));
  Multiplexer #(.disabled(0), .enable("false")) multiplexer_26 (
    .in0(multiplexer_10_out), .in1(multiplexer_12_out), .out(multiplexer_26_out), .sel(shamt[1]));
  Multiplexer #(.disabled(0), .enable("false")) multiplexer_27 (
    .in0(multiplexer_11_out), .in1(multiplexer_13_out), .out(multiplexer_27_out), .sel(shamt[1]));
  Multiplexer #(.disabled(0), .enable("false")) multiplexer_28 (
    .in0(multiplexer_12_out), .in1(multiplexer_14_out), .out(multiplexer_28_out), .sel(shamt[1]));
  Multiplexer #(.disabled(0), .enable("false")) multiplexer_29 (
    .in0(multiplexer_13_out), .in1(multiplexer_15_out), .out(multiplexer_29_out), .sel(shamt[1]));
  Multiplexer #(.disabled(0), .enable("false")) multiplexer_30 (
    .in0(multiplexer_14_out), .in1(multiplexer_16_out), .out(multiplexer_30_out), .sel(shamt[1]));
  Multiplexer #(.disabled(0), .enable("false")) multiplexer_31 (
    .in0(multiplexer_15_out), .in1(1'b0), .out(multiplexer_31_out), .sel(shamt[1]));
  Multiplexer #(.disabled(0), .enable("false")) multiplexer_32 (
    .in0(multiplexer_16_out), .in1(1'b0), .out(multiplexer_32_out), .sel(shamt[1]));
  Multiplexer #(.disabled(0), .enable("false")) multiplexer_33 (
    .in0(multiplexer_17_out), .in1(multiplexer_18_out), .out(\output [15]), .sel(shamt[0]));
  Multiplexer #(.disabled(0), .enable("false")) multiplexer_34 (
    .in0(multiplexer_18_out), .in1(multiplexer_19_out), .out(\output [14]), .sel(shamt[0]));
  Multiplexer #(.disabled(0), .enable("false")) multiplexer_35 (
    .in0(multiplexer_19_out), .in1(multiplexer_20_out), .out(\output [13]), .sel(shamt[0]));
  Multiplexer #(.disabled(0), .enable("false")) multiplexer_36 (
    .in0(multiplexer_20_out), .in1(multiplexer_21_out), .out(\output [12]), .sel(shamt[0]));
  Multiplexer #(.disabled(0), .enable("false")) multiplexer_37 (
    .in0(multiplexer_21_out), .in1(multiplexer_22_out), .out(\output [11]), .sel(shamt[0]));
  Multiplexer #(.disabled(0), .enable("false")) multiplexer_38 (
    .in0(multiplexer_22_out), .in1(multiplexer_23_out), .out(\output [10]), .sel(shamt[0]));
  Multiplexer #(.disabled(0), .enable("false")) multiplexer_39 (
    .in0(multiplexer_23_out), .in1(multiplexer_24_out), .out(\output [9]), .sel(shamt[0]));
  Multiplexer #(.disabled(0), .enable("false")) multiplexer_40 (
    .in0(multiplexer_24_out), .in1(multiplexer_25_out), .out(\output [8]), .sel(shamt[0]));
  Multiplexer #(.disabled(0), .enable("false")) multiplexer_41 (
    .in0(multiplexer_25_out), .in1(multiplexer_26_out), .out(\output [7]), .sel(shamt[0]));
  Multiplexer #(.disabled(0), .enable("false")) multiplexer_42 (
    .in0(multiplexer_26_out), .in1(multiplexer_27_out), .out(\output [6]), .sel(shamt[0]));
  Multiplexer #(.disabled(0), .enable("false")) multiplexer_43 (
    .in0(multiplexer_27_out), .in1(multiplexer_28_out), .out(\output [5]), .sel(shamt[0]));
  Multiplexer #(.disabled(0), .enable("false")) multiplexer_44 (
    .in0(multiplexer_28_out), .in1(multiplexer_29_out), .out(\output [4]), .sel(shamt[0]));
  Multiplexer #(.disabled(0), .enable("false")) multiplexer_45 (
    .in0(multiplexer_29_out), .in1(multiplexer_30_out), .out(\output [3]), .sel(shamt[0]));
  Multiplexer #(.disabled(0), .enable("false")) multiplexer_46 (
    .in0(multiplexer_30_out), .in1(multiplexer_31_out), .out(\output [2]), .sel(shamt[0]));
  Multiplexer #(.disabled(0), .enable("false")) multiplexer_47 (
    .in0(multiplexer_31_out), .in1(multiplexer_32_out), .out(\output [1]), .sel(shamt[0]));
  Multiplexer #(.disabled(0), .enable("false")) multiplexer_48 (
    .in0(multiplexer_32_out), .in1(1'b0), .out(\output [0]), .sel(shamt[0]));

  // Other names for the same wires on the sheet: _0 = \input [0]; _1 = \input [1]; _2 = \input [2]; _3 = \input [3];
  //   _4 = \input [4]; _5 = \input [5]; _6 = \input [6]; _7 = \input [7]; _8 = \input [8]; _9 = \input [9];
  //   _10 = \input [10]; _11 = \input [11]; _12 = \input [12]; _13 = \input [13]; _14 = \input [14];
  //   _15 = \input [15]; s0 = shamt[0]; s1 = shamt[1]; s2 = shamt[2]
endmodule

module shifter (
  input  [15:0] \input ,
  input  srl,
  input  [2:0] shamt,
  output [15:0] \output 
);

  wire in0, in1, in2, in3, in4, in5, in6, in7, in8, in9, in10, in11, in12, in13, in14, in15, out0, out1,
       out2, out3, out4, out5, out6, out7, out8, out9, out10, out11, out12, out13, out14, out15;

  Multiplexer #(.disabled(0), .enable("false")) multiplexer_1 (
    .in0(\input [15]), .in1(\input [0]), .out(in15), .sel(srl));
  Multiplexer #(.disabled(0), .enable("false")) multiplexer_2 (
    .in0(\input [14]), .in1(\input [1]), .out(in14), .sel(srl));
  Multiplexer #(.disabled(0), .enable("false")) multiplexer_3 (
    .in0(\input [13]), .in1(\input [2]), .out(in13), .sel(srl));
  Multiplexer #(.disabled(0), .enable("false")) multiplexer_4 (
    .in0(\input [12]), .in1(\input [3]), .out(in12), .sel(srl));
  Multiplexer #(.disabled(0), .enable("false")) multiplexer_5 (
    .in0(\input [11]), .in1(\input [4]), .out(in11), .sel(srl));
  Multiplexer #(.disabled(0), .enable("false")) multiplexer_6 (
    .in0(\input [10]), .in1(\input [5]), .out(in10), .sel(srl));
  Multiplexer #(.disabled(0), .enable("false")) multiplexer_7 (
    .in0(\input [9]), .in1(\input [6]), .out(in9), .sel(srl));
  Multiplexer #(.disabled(0), .enable("false")) multiplexer_8 (
    .in0(\input [8]), .in1(\input [7]), .out(in8), .sel(srl));
  Multiplexer #(.disabled(0), .enable("false")) multiplexer_9 (
    .in0(\input [7]), .in1(\input [8]), .out(in7), .sel(srl));
  Multiplexer #(.disabled(0), .enable("false")) multiplexer_10 (
    .in0(\input [6]), .in1(\input [9]), .out(in6), .sel(srl));
  Multiplexer #(.disabled(0), .enable("false")) multiplexer_11 (
    .in0(\input [5]), .in1(\input [10]), .out(in5), .sel(srl));
  Multiplexer #(.disabled(0), .enable("false")) multiplexer_12 (
    .in0(\input [4]), .in1(\input [11]), .out(in4), .sel(srl));
  Multiplexer #(.disabled(0), .enable("false")) multiplexer_13 (
    .in0(\input [3]), .in1(\input [12]), .out(in3), .sel(srl));
  Multiplexer #(.disabled(0), .enable("false")) multiplexer_14 (
    .in0(\input [2]), .in1(\input [13]), .out(in2), .sel(srl));
  Multiplexer #(.disabled(0), .enable("false")) multiplexer_15 (
    .in0(\input [1]), .in1(\input [14]), .out(in1), .sel(srl));
  Multiplexer #(.disabled(0), .enable("false")) multiplexer_16 (
    .in0(\input [0]), .in1(\input [15]), .out(in0), .sel(srl));
  shift_left shift_left_1 (
    .\input ({in15, in14, in13, in12, in11, in10, in9, in8, in7, in6, in5, in4, in3, in2, in1, in0}),
    .shamt(shamt),
    .\output ({out15, out14, out13, out12, out11, out10, out9, out8, out7, out6, out5, out4, out3, out2, out1, out0}));
  Multiplexer #(.disabled(0), .enable("false")) multiplexer_17 (.in0(out15), .in1(out0), .out(\output [15]), .sel(srl));
  Multiplexer #(.disabled(0), .enable("false")) multiplexer_18 (.in0(out14), .in1(out1), .out(\output [14]), .sel(srl));
  Multiplexer #(.disabled(0), .enable("false")) multiplexer_19 (.in0(out13), .in1(out2), .out(\output [13]), .sel(srl));
  Multiplexer #(.disabled(0), .enable("false")) multiplexer_20 (.in0(out12), .in1(out3), .out(\output [12]), .sel(srl));
  Multiplexer #(.disabled(0), .enable("false")) multiplexer_21 (.in0(out11), .in1(out4), .out(\output [11]), .sel(srl));
  Multiplexer #(.disabled(0), .enable("false")) multiplexer_22 (.in0(out10), .in1(out5), .out(\output [10]), .sel(srl));
  Multiplexer #(.disabled(0), .enable("false")) multiplexer_23 (.in0(out9), .in1(out6), .out(\output [9]), .sel(srl));
  Multiplexer #(.disabled(0), .enable("false")) multiplexer_24 (.in0(out8), .in1(out7), .out(\output [8]), .sel(srl));
  Multiplexer #(.disabled(0), .enable("false")) multiplexer_25 (.in0(out7), .in1(out8), .out(\output [7]), .sel(srl));
  Multiplexer #(.disabled(0), .enable("false")) multiplexer_26 (.in0(out6), .in1(out9), .out(\output [6]), .sel(srl));
  Multiplexer #(.disabled(0), .enable("false")) multiplexer_27 (.in0(out5), .in1(out10), .out(\output [5]), .sel(srl));
  Multiplexer #(.disabled(0), .enable("false")) multiplexer_28 (.in0(out4), .in1(out11), .out(\output [4]), .sel(srl));
  Multiplexer #(.disabled(0), .enable("false")) multiplexer_29 (.in0(out3), .in1(out12), .out(\output [3]), .sel(srl));
  Multiplexer #(.disabled(0), .enable("false")) multiplexer_30 (.in0(out2), .in1(out13), .out(\output [2]), .sel(srl));
  Multiplexer #(.disabled(0), .enable("false")) multiplexer_31 (.in0(out1), .in1(out14), .out(\output [1]), .sel(srl));
  Multiplexer #(.disabled(0), .enable("false")) multiplexer_32 (.in0(out0), .in1(out15), .out(\output [0]), .sel(srl));

  // Other names for the same wires on the sheet: _0 = \input [0]; _1 = \input [1]; _2 = \input [2]; _3 = \input [3];
  //   _4 = \input [4]; _5 = \input [5]; _6 = \input [6]; _7 = \input [7]; _8 = \input [8]; _9 = \input [9];
  //   _10 = \input [10]; _11 = \input [11]; _12 = \input [12]; _13 = \input [13]; _14 = \input [14];
  //   _15 = \input [15]
endmodule
